// Logisim project 1bit_CPU.circ as structural Verilog: 4 circuits, main circuit One_Bit_CPU
module CPU_and_ProgramRom (
);

  wire MasterClock_out, por_1_out;
  wire [7:0] ProgramROM_data;
  wire [11:0] one_bit_cpu_1_instructionaddress;

  Clock #(.highDuration(2), .lowDuration(2)) MasterClock (.out(MasterClock_out));
  POR por_1 (.out(por_1_out));
  ROM #(.addrWidth(12)) ProgramROM (.addr(one_bit_cpu_1_instructionaddress), .data(ProgramROM_data));
  One_Bit_CPU one_bit_cpu_1 (
    .Reset(por_1_out), .Clock(MasterClock_out), .InstructionIn(ProgramROM_data),
    .InstructionAddress(one_bit_cpu_1_instructionaddress));  // open: DataIn, DataOut, Write, DataAddress

  // Notes on the sheet:
  //   contents of ProgramROM (hex, n*v repeats v):
  //   8c 60 f0 5 61 63
endmodule

module One_Bit_CPU (
  input  Reset,
  input  Clock,
  input  DataIn,
  input  [7:0] InstructionIn,
  output DataOut,
  output Write,
  output [10:0] DataAddress,
  output [11:0] InstructionAddress
);

  wire Accumulator_q, bitselector_1_out, Clk2, FetchNext_qn, not_3_out;
  wire [2:0] StackPointer_q;
  wire [3:0] and_1_out;
  wire [6:0] FetchNext_q;
  wire [11:0] InstructionRegister_q, multiplexer_1_out, ProgramStack_dout;
  wire [17:0] Microcode_data;

  not not_1 (Clk2, Clock);
  ROM #(.addrWidth(7), .dataWidth(18)) Microcode (
    .addr({FetchNext_q[6:3], InstructionRegister_q[11:10], FetchNext_q[0]}), .data(Microcode_data));
  Counter #(.max('h7), .width(3)) StackPointer (
    .clr(Reset), .load(Microcode_data[16]), .up(Microcode_data[17]), .count(1'b1), .clk(Clock),
    .Q(StackPointer_q));  // open: D, carry
  // Probe on Microcode_data
  and and_1 (and_1_out[0], and_1_out[3], Accumulator_q);
  or or_1 (and_1_out[1], and_1_out[3], Accumulator_q);
  not not_2 (and_1_out[2], Accumulator_q);
  RAM #(.addrWidth(3), .dataWidth(12)) ProgramStack (
    .addr(StackPointer_q), .we(Microcode_data[14]), .oe(Microcode_data[15]), .din(InstructionAddress),
    .dout(ProgramStack_dout));  // open: clk
  T_Flip_Flop FetchNext (
    .T(Microcode_data[13]), .clk(Clk2), .Q(FetchNext_q[0]), .Qn(FetchNext_qn), .reset(Reset));  // open: preset
  Register #(.width(1)) Accumulator (
    .D(bitselector_1_out), .en(Microcode_data[3]), .clk(Clk2), .Q(Accumulator_q), .clr(Reset));
  BitSelector #(.width(7)) bitselector_1 (
    .in({2'b01, DataIn, and_1_out}), .out(bitselector_1_out), .sel(Microcode_data[2:0]));
  Register ExtraByte (.D(InstructionIn), .en(FetchNext_q[0]), .clk(Clock), .Q(InstructionRegister_q[7:0]), .clr(Reset));
  Register InstructionRegister (
    .D(InstructionIn), .en(FetchNext_qn), .clk(Clock), .Q({FetchNext_q[6:3], InstructionRegister_q[11:8]}),
    .clr(Reset));
  Multiplexer #(.width(12)) multiplexer_1 (
    .in0(InstructionRegister_q), .in1(ProgramStack_dout), .out(multiplexer_1_out), .sel(Microcode_data[12]));
  Counter #(.max('hfff), .width(12)) ProgramCounter (
    .clr(Reset), .load(Microcode_data[10]), .up(not_3_out), .count(1'b1), .clk(Clk2), .D(multiplexer_1_out),
    .Q(InstructionAddress));  // open: carry
  not not_3 (not_3_out, Microcode_data[11]);
  RegisterBank32 Registers (
    .Address({FetchNext_q[3], InstructionRegister_q[11:8]}), .DataIn(Accumulator_q),
    .Write(Microcode_data[4]), .Clk(Clk2), .Reset(Reset), .DataOut(and_1_out[3]));
  Counter #(.max('h7ff), .width(11)) AddressLatch_IncDec (
    .clr(Reset), .load(Microcode_data[8]), .up(Microcode_data[9]), .count(1'b1), .clk(Clk2),
    .D(InstructionRegister_q[10:0]), .Q(DataAddress));  // open: carry
  Register #(.width(1)) DataOutLatch (.D(Accumulator_q), .en(Microcode_data[6]), .clk(Clk2), .Q(DataOut), .clr(Reset));
  Register #(.width(1)) WriteLatch (
    .D(InstructionRegister_q[11]), .en(Microcode_data[7]), .clk(Clk2), .Q(Write), .clr(Reset));

  // Other names for the same wires on the sheet: Clk1 = Clock; Rst = Reset

  // Notes on the sheet:
  //   contents of Microcode (hex, n*v repeats v):
  //   8 0 8 0 8 0 8 0 8 0 8 0 8 0 8 0 9 0 9 0 9 0 9 0 9 0 9 0 9 0 9 0 b 0 b 0 b 0 b 0 b 0 b 0 b 0 b 0 10 0
  //   10 0 10 0 10 0 10 0 10 0 10 0 10 0 a 0 0 0 e 0 d 49*0 2000 2400 2000 2400 2000 2400 2000 2400
endmodule

module RegisterBank8 (
  input  [2:0] Address,
  input  DataIn,
  input  Clk,
  input  Write,
  input  Reset,
  output DataOut
);

  wire and_1_out, d_ff_1_q, d_ff_2_q, d_ff_3_q, d_ff_4_q, d_ff_5_q, d_ff_6_q, d_ff_7_q, d_ff_8_q,
       demultiplexer_1_out0, demultiplexer_1_out1, demultiplexer_1_out2, demultiplexer_1_out3,
       demultiplexer_1_out4, demultiplexer_1_out5, demultiplexer_1_out6, demultiplexer_1_out7;

  and and_1 (and_1_out, Clk, Write);
  Demultiplexer #(.select(3)) demultiplexer_1 (
    .out0(demultiplexer_1_out0), .out1(demultiplexer_1_out1), .out2(demultiplexer_1_out2),
    .out3(demultiplexer_1_out3), .out4(demultiplexer_1_out4), .out5(demultiplexer_1_out5),
    .out6(demultiplexer_1_out6), .out7(demultiplexer_1_out7), .in(and_1_out), .sel(Address));
  D_Flip_Flop d_ff_1 (.D(DataIn), .clk(demultiplexer_1_out0), .Q(d_ff_1_q), .reset(Reset));  // open: Qn, preset
  D_Flip_Flop d_ff_2 (.D(DataIn), .clk(demultiplexer_1_out1), .Q(d_ff_2_q), .reset(Reset));  // open: Qn, preset
  D_Flip_Flop d_ff_3 (.D(DataIn), .clk(demultiplexer_1_out2), .Q(d_ff_3_q), .reset(Reset));  // open: Qn, preset
  D_Flip_Flop d_ff_4 (.D(DataIn), .clk(demultiplexer_1_out3), .Q(d_ff_4_q), .reset(Reset));  // open: Qn, preset
  D_Flip_Flop d_ff_5 (.D(DataIn), .clk(demultiplexer_1_out4), .Q(d_ff_5_q), .reset(Reset));  // open: Qn, preset
  D_Flip_Flop d_ff_6 (.D(DataIn), .clk(demultiplexer_1_out5), .Q(d_ff_6_q), .reset(Reset));  // open: Qn, preset
  D_Flip_Flop d_ff_7 (.D(DataIn), .clk(demultiplexer_1_out6), .Q(d_ff_7_q), .reset(Reset));  // open: Qn, preset
  D_Flip_Flop d_ff_8 (.D(DataIn), .clk(demultiplexer_1_out7), .Q(d_ff_8_q), .reset(Reset));  // open: Qn, preset
  Multiplexer #(.select(3)) multiplexer_1 (
    .in0(d_ff_1_q), .in1(d_ff_2_q), .in2(d_ff_3_q), .in3(d_ff_4_q), .in4(d_ff_5_q), .in5(d_ff_6_q),
    .in6(d_ff_7_q), .in7(d_ff_8_q), .out(DataOut), .sel(Address));
endmodule

module RegisterBank32 (
  input  [4:0] Address,
  input  DataIn,
  input  Write,
  input  Clk,
  input  Reset,
  output DataOut
);

  wire and_1_out, demultiplexer_1_out0, demultiplexer_1_out1, demultiplexer_1_out2, demultiplexer_1_out3,
       registerbank8_1_dataout, registerbank8_2_dataout, registerbank8_4_dataout, registerbank8_5_dataout;

  and and_1 (and_1_out, Write, Clk);
  Demultiplexer #(.select(2)) demultiplexer_1 (
    .out0(demultiplexer_1_out0), .out1(demultiplexer_1_out1), .out2(demultiplexer_1_out2),
    .out3(demultiplexer_1_out3), .in(and_1_out), .sel(Address[4:3]));
  RegisterBank8 registerbank8_1 (
    .Address(Address[2:0]), .DataIn(DataIn), .Clk(demultiplexer_1_out0), .Write(Write), .Reset(Reset),
    .DataOut(registerbank8_1_dataout));
  RegisterBank8 registerbank8_2 (
    .Address(Address[2:0]), .DataIn(DataIn), .Clk(demultiplexer_1_out1), .Write(Write), .Reset(Reset),
    .DataOut(registerbank8_2_dataout));
  RegisterBank8 registerbank8_3 (
    .Address(Address[2:0]), .DataIn(DataIn), .Clk(demultiplexer_1_out1), .Write(Write), .Reset(Reset),
    .DataOut(registerbank8_2_dataout));
  RegisterBank8 registerbank8_4 (
    .Address(Address[2:0]), .DataIn(DataIn), .Clk(demultiplexer_1_out2), .Write(Write), .Reset(Reset),
    .DataOut(registerbank8_4_dataout));
  RegisterBank8 registerbank8_5 (
    .Address(Address[2:0]), .DataIn(DataIn), .Clk(demultiplexer_1_out3), .Write(Write), .Reset(Reset),
    .DataOut(registerbank8_5_dataout));
  Multiplexer #(.select(2)) multiplexer_1 (
    .in0(registerbank8_1_dataout), .in1(registerbank8_2_dataout), .in2(registerbank8_4_dataout),
    .in3(registerbank8_5_dataout), .out(DataOut), .sel(Address[4:3]));
endmodule
