// Logisim project InstructionDecoder.circ as structural Verilog
module opcode2instr (
  input  b7,
  input  b6,
  input  b5,
  input  b4,
  input  b3,
  input  b2,
  output c_and,
  output c_or,
  output c_load,
  output c_save,
  output c_not,
  output c_zero,
  output c_one,
  output c_ret,
  output c_out,
  output c_outinc,
  output c_outdec,
  output c_in,
  output c_ininc,
  output c_indec,
  output c_infrom,
  output c_outto,
  output c_call,
  output c_jmpt,
  output c_jmp
);

  wire not_1_out, not_2_out, not_3_out, not_4_out, not_5_out, not_6_out;

  not not_1 (not_1_out, b7);
  not not_2 (not_2_out, b6);
  not not_3 (not_3_out, b5);
  not not_4 (not_4_out, b4);
  not not_5 (not_5_out, b3);
  not not_6 (not_6_out, b2);
  and and_1 (c_and, not_1_out, not_2_out, not_3_out);
  and and_2 (c_or, not_1_out, not_2_out, b5);
  and and_3 (c_load, not_1_out, b6, not_3_out);
  and and_4 (c_save, not_1_out, b6, b5);
  and and_5 (c_not, b7, not_2_out, not_3_out, not_4_out, not_5_out, not_6_out);
  and and_6 (c_zero, b7, not_2_out, not_3_out, not_4_out, b3, not_6_out);
  and and_7 (c_one, b7, not_2_out, not_3_out, not_4_out, b3, b2);
  and and_8 (c_ret, b7, not_2_out, not_3_out, b4, not_5_out, not_6_out);
  and and_9 (c_out, b7, not_2_out, b5, not_4_out, not_5_out, not_6_out);
  and and_10 (c_outinc, b7, not_2_out, b5, not_4_out, b3, not_6_out);
  and and_11 (c_outdec, b7, not_2_out, b5, not_4_out, b3, b2);
  and and_12 (c_in, b7, not_2_out, b5, b4, not_5_out, not_6_out);
  and and_13 (c_ininc, b7, not_2_out, b5, b4, b3, not_6_out);
  and and_14 (c_indec, b7, not_2_out, b5, b4, b3, b2);
  and and_15 (c_infrom, b7, b6, not_3_out, not_4_out, not_5_out);
  and and_16 (c_outto, b7, b6, not_3_out, not_4_out, b3);
  and and_17 (c_call, b7, b6, not_3_out, b4);
  and and_18 (c_jmpt, b7, b6, b5, not_4_out);
  and and_19 (c_jmp, b7, b6, b5, b4);
endmodule
