// Digital circuit MC14500-test.dig as structural Verilog
module MC14500_test (
  input  Data,
  input  Clk,
  input  RST,
  output Write,
  output RR,
  output JMP,
  output RTN,
  output FLG0,
  output FLGF
);

  wire mc14500_1_x1;
  wire [3:0] counter_1_out, rom_1_d;

  Counter #(.Bits(4), .isProgramCounter("true")) counter_1 (
    .en(1'b1), .C(mc14500_1_x1), .clr(RST), .out(counter_1_out));  // open: ovf
  // Probe A on counter_1_out
  ROM #(.AddrBits(4), .isProgramMemory("true"), .Bits(4)) rom_1 (.A(counter_1_out), .sel(1'b1), .D(rom_1_d));
  // Probe I on rom_1_d
  MC14500 mc14500_1 (
    .Data(Data), .I(rom_1_d), .X2(Clk), .RST(RST), .Write(Write), .RR(RR), .JMP(JMP), .RTN(RTN), .FLG0(FLG0),
    .FLGF(FLGF), .X1(mc14500_1_x1));
  // Probe X1 on mc14500_1_x1

  // Notes on the sheet:
  //   Clk: Hz: 2147483647
endmodule

/* Test case Test flags:
Clk X1 RST  A I   Data Write RR JMP RTN FLG0 FLGF

#       NOP0, NOPF, JMP
program(0,0xf,0xc) 

# Reset
0   X  1    0 0     z   0     0  0   0   0    0
C   X  1    0 0     z   0     0  0   0   0    0
0   X  0    0 0     z   0     0  0   0   0    0
C   X  0    X X     z   0     0  0   0   1    0
0   X  0    1 0xf   z   0     0  0   0   0    1
C   X  0    X X     z   0     0  0   0   0    0
0   X  0    2 0xc   z   0     0  1   0   0    0
*/
