// Digital circuit MC14512.dig as structural Verilog
module MC14512 (
  input  A,
  input  B,
  input  C,
  input  [7:0] X,
  input  INH,
  input  DIS,
  output Z
);

  wire and_1_out, bitselector_1_out, not_1_out, not_2_out;

  not not_1 (not_1_out, INH);
  not not_2 (not_2_out, DIS);
  BitSelector #(.Selector_Bits(3)) bitselector_1 (.in(X), .sel({C, B, A}), .out(bitselector_1_out));
  and and_1 (and_1_out, bitselector_1_out, not_1_out);
  assign Z = not_2_out ? and_1_out : 1'bz;  // Driver driver_1

  // Notes on the sheet:
  //   A: pin 11
  //   B: pin 12
  //   C: pin 13
  //   X: pin 1,2,3,4,5,6,7,9
  //   INH: pin 10
  //   DIS: pin 15
  //   Z: pin 14
endmodule
